// Digital circuit Circuito.dig as structural Verilog
module Circuito (
  input  A0,
  input  A1,
  input  A2,
  input  A3,
  input  A4,
  input  A5,
  input  B0,
  input  B1,
  input  B2,
  input  B3,
  input  B4,
  input  B5,
  input  O0,
  input  O1,
  output S0,
  output S1,
  output S2,
  output S3,
  output S4,
  output S5,
  output S6,
  output S7,
  output F
);

  wire C0, M0, M1, M2, M3, M4, M5, MF, SB0, SB1, SB2, SB3, SB4, SB5, SBF, SM0, SM1, SM2, SM3, SM4, SM5, SMF;

  SomaCompleta somacompleta_1 (
    .A0(A0), .A1(A1), .A2(A2), .A3(A3), .A4(A4), .A5(A5), .B0(B0), .B1(B1), .B2(B2), .B3(B3), .B4(B4),
    .B5(B5), .O0(O0), .O1(O1), .S0(SM0), .S1(SM1), .S2(SM2), .S3(SM3), .S4(SM4), .S5(SM5), .SF(SMF));
  SubCompleta subcompleta_1 (
    .A0(A0), .A1(A1), .A2(A2), .A3(A3), .A4(A4), .A5(A5), .B0(B0), .B1(B1), .B2(B2), .B3(B3), .B4(B4),
    .B5(B5), .O0(O0), .O1(O1), .SB0(SB0), .SB1(SB1), .SB2(SB2), .SB3(SB3), .SB4(SB4), .SB5(SB5), .SBF(SBF));
  CompCompleta compcompleta_1 (
    .A0(A0), .A1(A1), .A2(A2), .A3(A3), .A4(A4), .A5(A5), .B0(B0), .B1(B1), .B2(B2), .B3(B3), .B4(B4),
    .B5(B5), .O0(O0), .O1(O1), .C0(C0));
  MultCompleta multcompleta_1 (
    .A0(A0), .A1(A1), .A2(A2), .A3(A3), .A4(A4), .A5(A5), .B0(B0), .B1(B1), .B2(B2), .B3(B3), .B4(B4),
    .B5(B5), .O0(O0), .O1(O1), .M0(M0), .M1(M1), .M2(M2), .M3(M3), .M4(M4), .M5(M5), .M6(S6), .M7(S7), .MF(MF));
  or or_1 (F, SMF, SBF, MF);
  or or_2 (S5, SM5, SB5, M5);
  or or_3 (S4, SM4, SB4, M4);
  or or_4 (S3, SM3, SB3, M3);
  or or_5 (S2, SM2, SB2, M2);
  or or_6 (S1, SM1, SB1, M1);
  or or_7 (S0, SM0, SB0, C0, M0);

  // Other names for the same wires on the sheet: M6 = S6; M7 = S7; SF = F
endmodule
