// Digital circuit CompCompleta.dig as structural Verilog
module CompCompleta (
  input  A0,
  input  A1,
  input  A2,
  input  A3,
  input  A4,
  input  A5,
  input  B0,
  input  B1,
  input  B2,
  input  B3,
  input  B4,
  input  B5,
  input  O0,
  input  O1,
  output C0
);

  wire not_1_out, not_2_out, not_3_out, S0, Z2;

  and and_1 (C0, Z2, S0);
  Comparar comparar_1 (
    .A0(A0), .B0(B0), .A1(A1), .B1(B1), .A2(A2), .B2(B2), .A3(A3), .B3(B3), .A4(A4), .B4(B4), .A5(A5),
    .B5(B5), .S0(S0));
  not not_1 (not_1_out, O0);
  not not_2 (not_2_out, O0);
  not not_3 (not_3_out, O0);
  Mux mux_1 (.X3(O0), .X2(not_3_out), .X1(not_2_out), .X0(not_1_out), .O1(O1), .O0(O0), .Z(Z2));
endmodule
