// Digital circuit Comparar.dig as structural Verilog
module Comparar (
  input  A0,
  input  B0,
  input  A1,
  input  B1,
  input  A2,
  input  B2,
  input  A3,
  input  B3,
  input  A4,
  input  B4,
  input  A5,
  input  B5,
  output S0
);

  wire and_1_out, and_2_out, xnor_1_out, xnor_2_out, xnor_3_out, xnor_4_out, xnor_5_out, xnor_6_out;

  xnor xnor_1 (xnor_1_out, A0, B0);
  xnor xnor_2 (xnor_2_out, A1, B1);
  xnor xnor_3 (xnor_3_out, A2, B2);
  xnor xnor_4 (xnor_4_out, A3, B3);
  xnor xnor_5 (xnor_5_out, A4, B4);
  xnor xnor_6 (xnor_6_out, A5, B5);
  and and_1 (and_1_out, xnor_1_out, xnor_2_out, xnor_3_out);
  and and_2 (and_2_out, xnor_4_out, xnor_5_out, xnor_6_out);
  and and_3 (S0, and_1_out, and_2_out);
endmodule
