// Digital circuit FA2.dig as structural Verilog
module FA2 (
  input  A,
  input  B,
  input  Cin,
  output S
);

  wire xor_1_out;

  xor xor_1 (xor_1_out, B, Cin);
  xor xor_2 (S, A, xor_1_out);
endmodule
