// Digital circuit MultCompleta.dig as structural Verilog
module MultCompleta (
  input  A0,
  input  A1,
  input  A2,
  input  A3,
  input  A4,
  input  A5,
  input  B0,
  input  B1,
  input  B2,
  input  B3,
  input  B4,
  input  B5,
  input  O0,
  input  O1,
  output M0,
  output M1,
  output M2,
  output M3,
  output M4,
  output M5,
  output M6,
  output M7,
  output MF
);

  wire not_1_out, S0, S1, S2, S3, S4, S5, S6, S7, SF, Z3;

  Multiplicador multiplicador_1 (
    .A3(A3), .A2(A2), .A1(A1), .A0(A0), .B0(B0), .B1(B1), .B2(B2), .B3(B3), .A4(A4), .A5(A5), .B4(B4),
    .B5(B5), .M0(S0), .M1(S1), .M2(S2), .M3(S3), .M4(S4), .M5(S5), .M6(S6), .M7(S7), .F(SF));
  MultPeloMuxV2 multpelomuxv2_1 (
    .Z0(Z3), .SM0(S0), .SM1(S1), .SM2(S2), .SM3(S3), .SM4(S4), .SM5(S5), .SMF(S6), .SM6(S7), .SM7(SF),
    .S0(M0), .S1(M1), .S2(M2), .S3(M3), .S4(M4), .S5(M5), .SF(M6), .S6(M7), .S7(MF));
  not not_1 (not_1_out, O0);
  Mux mux_1 (.X3(O0), .X2(not_1_out), .X1(O0), .X0(O0), .O1(O1), .O0(O0), .Z(Z3));
endmodule
