// Digital circuit MultPeloMux.dig as structural Verilog
module MultPeloMux (
  input  Z0,
  input  SM0,
  input  SM1,
  input  SM2,
  input  SM3,
  input  SM4,
  input  SM5,
  input  SMF,
  output S0,
  output S1,
  output S2,
  output S3,
  output S4,
  output S5,
  output SF
);

  and and_1 (SF, Z0, SMF);
  and and_2 (S5, Z0, SM5);
  and and_3 (S4, Z0, SM4);
  and and_4 (S3, Z0, SM3);
  and and_5 (S2, Z0, SM2);
  and and_6 (S1, Z0, SM1);
  and and_7 (S0, Z0, SM0);
endmodule
