// Digital circuit MultPeloMuxV2.dig as structural Verilog
module MultPeloMuxV2 (
  input  Z0,
  input  SM0,
  input  SM1,
  input  SM2,
  input  SM3,
  input  SM4,
  input  SM5,
  input  SMF,
  input  SM6,
  input  SM7,
  output S0,
  output S1,
  output S2,
  output S3,
  output S4,
  output S5,
  output SF,
  output S6,
  output S7
);

  and and_1 (SF, Z0, SMF);
  and and_2 (S7, Z0, SM7);
  and and_3 (S6, Z0, SM6);
  and and_4 (S5, Z0, SM5);
  and and_5 (S4, Z0, SM4);
  and and_6 (S3, Z0, SM3);
  and and_7 (S2, Z0, SM2);
  and and_8 (S1, Z0, SM1);
  and and_9 (S0, Z0, SM0);
endmodule
