// Digital circuit Multiplicador.dig as structural Verilog
module Multiplicador (
  input  A3,
  input  A2,
  input  A1,
  input  A0,
  input  B0,
  input  B1,
  input  B2,
  input  B3,
  input  A4,
  input  A5,
  input  B4,
  input  B5,
  output M0,
  output M1,
  output M2,
  output M3,
  output M4,
  output M5,
  output M6,
  output M7,
  output F
);

  wire and_2_out, and_3_out, and_4_out, and_5_out, and_6_out, and_7_out, and_8_out, and_9_out, and_10_out,
       and_11_out, and_12_out, and_13_out, and_14_out, and_15_out, and_16_out, fa_1_cout, fa_1_s, fa_2_cout,
       fa_2_s, fa_3_cout, fa_3_s, fa_4_cout, fa_4_s, fa_5_cout, fa_5_s, fa_6_cout, fa_7_cout, ha_1_cout,
       ha_2_cout, ha_2_s, ha_3_cout, ha_4_cout;

  or or_1 (F, A4, A5, B4, B5);
  and and_1 (M0, A0, B0);
  and and_2 (and_2_out, A1, B0);
  and and_3 (and_3_out, A2, B0);
  and and_4 (and_4_out, A3, B0);
  and and_5 (and_5_out, A0, B1);
  and and_6 (and_6_out, A1, B1);
  and and_7 (and_7_out, A2, B1);
  and and_8 (and_8_out, A3, B1);
  HA ha_1 (.A(and_5_out), .B(and_2_out), .S(M1), .Cout(ha_1_cout));
  FA fa_1 (.A(and_6_out), .B(and_3_out), .Cin(ha_1_cout), .S(fa_1_s), .Cout(fa_1_cout));
  FA fa_2 (.A(and_7_out), .B(and_4_out), .Cin(fa_1_cout), .S(fa_2_s), .Cout(fa_2_cout));
  HA ha_2 (.A(and_8_out), .B(fa_2_cout), .S(ha_2_s), .Cout(ha_2_cout));
  and and_9 (and_9_out, A0, B2);
  and and_10 (and_10_out, A1, B2);
  and and_11 (and_11_out, A2, B2);
  and and_12 (and_12_out, A3, B2);
  HA ha_3 (.A(and_9_out), .B(fa_1_s), .S(M2), .Cout(ha_3_cout));
  FA fa_3 (.A(and_10_out), .B(fa_2_s), .Cin(ha_3_cout), .S(fa_3_s), .Cout(fa_3_cout));
  FA fa_4 (.A(and_11_out), .B(ha_2_s), .Cin(fa_3_cout), .S(fa_4_s), .Cout(fa_4_cout));
  FA fa_5 (.A(and_12_out), .B(ha_2_cout), .Cin(fa_4_cout), .S(fa_5_s), .Cout(fa_5_cout));
  and and_13 (and_13_out, A0, B3);
  and and_14 (and_14_out, A1, B3);
  and and_15 (and_15_out, A2, B3);
  and and_16 (and_16_out, A3, B3);
  HA ha_4 (.A(and_13_out), .B(fa_3_s), .S(M3), .Cout(ha_4_cout));
  FA fa_6 (.A(and_14_out), .B(fa_4_s), .Cin(ha_4_cout), .S(M4), .Cout(fa_6_cout));
  FA fa_7 (.A(and_15_out), .B(fa_5_s), .Cin(fa_6_cout), .S(M5), .Cout(fa_7_cout));
  FA fa_8 (.A(and_16_out), .B(fa_5_cout), .Cin(fa_7_cout), .S(M6), .Cout(M7));
endmodule
