// Digital circuit Mux.dig as structural Verilog
module Mux (
  input  X3,
  input  X2,
  input  X1,
  input  X0,
  input  O1,
  input  O0,
  output Z
);

  wire and_1_out, and_2_out, and_3_out, and_4_out, not_1_out, not_2_out, not_3_out;

  not not_1 (not_1_out, O1);
  not not_2 (not_2_out, O0);
  not not_3 (not_3_out, O0);
  and and_1 (and_1_out, X3, not_1_out, not_2_out);
  and and_2 (and_2_out, X2, not_1_out, O0);
  and and_3 (and_3_out, X1, O1, not_3_out);
  and and_4 (and_4_out, X0, O1, O0);
  or or_1 (Z, and_1_out, and_2_out, and_3_out, and_4_out);
endmodule
