// Digital circuit SomaCompleta.dig as structural Verilog
module SomaCompleta (
  input  A0,
  input  A1,
  input  A2,
  input  A3,
  input  A4,
  input  A5,
  input  B0,
  input  B1,
  input  B2,
  input  B3,
  input  B4,
  input  B5,
  input  O0,
  input  O1,
  output S0,
  output S1,
  output S2,
  output S3,
  output S4,
  output S5,
  output SF
);

  wire not_1_out, not_2_out, not_3_out, S0_t, S1_t, S2_t, S3_t, S4_t, S5_t, SF_t, Z0;

  MultPeloMux multpelomux_1 (
    .Z0(Z0), .SM0(S0_t), .SM1(S1_t), .SM2(S2_t), .SM3(S3_t), .SM4(S4_t), .SM5(S5_t), .SMF(SF_t), .S0(S0),
    .S1(S1), .S2(S2), .S3(S3), .S4(S4), .S5(S5), .SF(SF));
  Somador somador_1 (
    .A0(A0), .B0(B0), .A1(A1), .B1(B1), .A2(A2), .B2(B2), .A3(A3), .B3(B3), .A4(A4), .B4(B4), .A5(A5),
    .B5(B5), .s0(S0_t), .s1(S1_t), .s2(S2_t), .s3(S3_t), .s4(S4_t), .s5(S5_t), .F(SF_t));
  not not_1 (not_1_out, O0);
  not not_2 (not_2_out, O0);
  not not_3 (not_3_out, O0);
  Mux mux_1 (.X3(not_2_out), .X2(not_3_out), .X1(O0), .X0(not_1_out), .O1(O1), .O0(O0), .Z(Z0));

  // Other names for the same wires on the sheet: SM0 = S0; SM1 = S1; SM2 = S2; SM3 = S3; SM4 = S4; SM5 = S5; SMF = SF
endmodule
