// Digital circuit Somador.dig as structural Verilog
module Somador (
  input  A0,
  input  B0,
  input  A1,
  input  B1,
  input  A2,
  input  B2,
  input  A3,
  input  B3,
  input  A4,
  input  B4,
  input  A5,
  input  B5,
  output s0,
  output s1,
  output s2,
  output s3,
  output s4,
  output s5,
  output F
);

  wire fa_1_cout, fa_2_cout, fa_3_cout, fa_4_cout, ha_1_cout;

  FA2 fa2_1 (.A(A5), .B(B5), .Cin(fa_1_cout), .S(F));
  FA fa_1 (.A(A4), .B(B4), .Cin(fa_2_cout), .S(s4), .Cout(fa_1_cout));
  FA fa_2 (.A(A3), .B(B3), .Cin(fa_3_cout), .S(s3), .Cout(fa_2_cout));
  FA fa_3 (.A(A2), .B(B2), .Cin(fa_4_cout), .S(s2), .Cout(fa_3_cout));
  FA fa_4 (.A(A1), .B(B1), .Cin(ha_1_cout), .S(s1), .Cout(fa_4_cout));
  HA ha_1 (.A(A0), .B(B0), .S(s0), .Cout(ha_1_cout));

  assign s5 = F;
endmodule
