// Digital circuit Sub.dig as structural Verilog
module Sub (
  input  A0,
  input  A1,
  input  A2,
  input  A3,
  input  A4,
  input  A5,
  input  B1,
  input  B2,
  input  B3,
  input  B4,
  input  B5,
  input  B0,
  output s0,
  output F,
  output s1,
  output s2,
  output s3,
  output s4,
  output s5
);

  wire fa_2_cout, fa_3_cout, fa_4_cout, fa_5_cout, fa_6_cout, not_1_out, not_2_out, not_3_out, not_4_out,
       not_5_out, not_6_out;

  not not_1 (not_1_out, B5);
  FA fa_1 (.A(A5), .B(not_1_out), .Cin(fa_2_cout), .S(s5), .Cout(F));
  not not_2 (not_2_out, B4);
  FA fa_2 (.A(A4), .B(not_2_out), .Cin(fa_3_cout), .S(s4), .Cout(fa_2_cout));
  not not_3 (not_3_out, B3);
  FA fa_3 (.A(A3), .B(not_3_out), .Cin(fa_4_cout), .S(s3), .Cout(fa_3_cout));
  not not_4 (not_4_out, B2);
  FA fa_4 (.A(A2), .B(not_4_out), .Cin(fa_5_cout), .S(s2), .Cout(fa_4_cout));
  not not_5 (not_5_out, B1);
  FA fa_5 (.A(A1), .B(not_5_out), .Cin(fa_6_cout), .S(s1), .Cout(fa_5_cout));
  not not_6 (not_6_out, B0);
  FA fa_6 (.A(A0), .B(not_6_out), .Cin(1'b1), .S(s0), .Cout(fa_6_cout));
endmodule
