// Digital circuit SubCompleta.dig as structural Verilog
module SubCompleta (
  input  A0,
  input  A1,
  input  A2,
  input  A3,
  input  A4,
  input  A5,
  input  B0,
  input  B1,
  input  B2,
  input  B3,
  input  B4,
  input  B5,
  input  O0,
  input  O1,
  output SB0,
  output SB1,
  output SB2,
  output SB3,
  output SB4,
  output SB5,
  output SBF
);

  wire not_1_out, S0, S1, S2, S3, S4, S5, SF, Z1;

  MultPeloMux multpelomux_1 (
    .Z0(Z1), .SM0(S0), .SM1(S1), .SM2(S2), .SM3(S3), .SM4(S4), .SM5(S5), .SMF(SF), .S0(SB0), .S1(SB1),
    .S2(SB2), .S3(SB3), .S4(SB4), .S5(SB5), .SF(SBF));
  Sub sub_1 (
    .A0(A0), .A1(A1), .A2(A2), .A3(A3), .A4(A4), .A5(A5), .B1(B1), .B2(B2), .B3(B3), .B4(B4), .B5(B5),
    .B0(B0), .s0(S0), .F(SF), .s1(S1), .s2(S2), .s3(S3), .s4(S4), .s5(S5));
  not not_1 (not_1_out, O0);
  Mux mux_1 (.X3(O0), .X2(O0), .X1(O0), .X0(not_1_out), .O1(O1), .O0(O0), .Z(Z1));
endmodule
